# Fritzing sketch NOS01 (saved by Fritzing 0.9.3b)
breadboards: 1

parts:
  Q1 = NPN-Transistor [package="TO92 [THT]"]
  R1 = Resistor [tolerance=±5% resistance=10k package=THT]
  Q2 = NPN-Transistor [package="TO92 [THT]"]
  C1 = Film/Foil Capacitor [capacitance=100nF voltage=35V package="5mm [THT, pp]"]
  R2 = Resistor [tolerance=±5% resistance=100k package=THT]
  IC1 = Dual Op-Amp [package=dip08]
  R3 = Resistor [tolerance=±5% resistance=330k package=THT]
  R4 = Resistor [tolerance=±5% resistance=100k package=THT]
  C2 = Film/Foil Capacitor [capacitance=100nF voltage=35V package="5mm [THT, pp]"]
  R5 = Resistor [tolerance=±5% resistance=10k package=THT]
  R6 = TRIMPOT [package=3362u-2]
  R7 = Resistor [tolerance=±5% resistance=10k package=THT]
  IC2 = Dual Op-Amp [package=dip08]
  R8 = Resistor [tolerance=±5% resistance=1k package=THT]
  C3 = Film/Foil Capacitor [capacitance=100nF voltage=35V package="5mm [THT, pp]"]
  R9 = Resistor [tolerance=±5% resistance=1k package=THT]
  R10 = Resistor [tolerance=±5% resistance=10k package=THT]
  C4 = Film/Foil Capacitor [capacitance=100nF voltage=35V package="5mm [THT, pp]"]
  R11 = Resistor [tolerance=±5% resistance=22k package=THT]
  R12 = Resistor [tolerance=±5% resistance=10k package=THT]
  R13 = Resistor [tolerance=±5% resistance=100k package=THT]
  R14 = Resistor [tolerance=±5% resistance=10k package=THT]
  R15 = Resistor [tolerance=±5% resistance=1k package=THT]
  R16 = Resistor [tolerance=±5% resistance=1k package=THT]
  C5 = Ceramic Capacitor [capacitance=100nF package="100 mil [THT, multilayer]"]
  C6 = Ceramic Capacitor [capacitance=100nF package="100 mil [THT, multilayer]"]
  C7 = Ceramic Capacitor [capacitance=100nF package="100 mil [THT, multilayer]"]
  C8 = Ceramic Capacitor [capacitance=100nF package="100 mil [THT, multilayer]"]
  C9 = Electrolytic Capacitor [capacitance=1µF package="100 mil [THT, electrolytic]"]
  C10 = Electrolytic Capacitor [capacitance=1µF package="100 mil [THT, electrolytic]"]
  R17 = Resistor [tolerance=±5% resistance=1k package=THT]
  LED1 = LED - 3mm [color="Green (570nm)" package="3 mm [THT]"]

nets:
  N1: Q1.E, R1.Pin_1, Q2.B, C1.-
  N2: Q1.C, Q2.C
  N3: R1.Pin_0, IC1.A_V+, IC2.A_V+, C5.0, C6.0, C9.+, R17.Pin_0
  N4: Q2.E, IC1.A_V-, IC2.A_V-, C7.0, C8.0, C10.-, LED1.cathode
  N5: C1.+, R2.Pin_0, IC1.A_+IN
  N6: R2.Pin_1, R4.Pin_0, R5.Pin_1, R7.Pin_0, R9.Pin_0, C4.-, R12.Pin_0, R14.Pin_1, C5.1, C6.1, C7.1, C8.1, C9.-, C10.+
  N7: IC1.A_OUT, R3.Pin_0, C2.+
  N8: IC1.A_-IN, R3.Pin_1, R5.Pin_0
  N9: IC1.B_+IN, R4.Pin_1, C2.-
  N10: IC1.B_-IN, R6.CCW, R7.Pin_1
  N11: IC1.B_OUT, R6.WIPER, R6.CW, R8.Pin_0, C3.-, R10.Pin_0
  N12: IC2.A_OUT, R13.Pin_0, R16.Pin_0
  N13: IC2.A_-IN, R13.Pin_1, R14.Pin_0
  N14: IC2.A_+IN, R10.Pin_1, C4.+
  N15: IC2.B_+IN, C3.+, R9.Pin_1
  N16: IC2.B_-IN, R11.Pin_1, R12.Pin_1
  N17: IC2.B_OUT, R11.Pin_0, R15.Pin_0
  N18: R17.Pin_1, LED1.anode

notes:
  GND
  V+
  V-
  GND
  Blue
  White
  Pink
