# Fritzing sketch Noise Generator (saved by Fritzing 0.9.3b)
breadboards: 1

parts:
  Q1 = NPN-Transistor [package="TO92 [THT]"]
  R1 = Resistor [tolerance=±5% resistance=680 package=THT]
  Q2 = NPN-Transistor [package="TO92 [THT]"]
  R2 = Resistor [tolerance=±5% resistance=1k package=THT]
  C2 = Electrolytic Capacitor [capacitance=1µF package="100 mil [THT, electrolytic]"]
  R3 = Resistor [tolerance=±5% resistance=4.7k package=THT]
  C3 = Electrolytic Capacitor [capacitance=1µF package="100 mil [THT, electrolytic]"]
  R4 = Resistor [tolerance=±5% resistance=100k package=THT]
  C4 = Ceramic Capacitor [capacitance=100nF package="100 mil [THT, multilayer]"]

nets:
  N1: Q1.E, R1.Pin_1, C4.0
  N2: Q1.C, Q2.C
  N3: R1.Pin_0, R3.Pin_0, C4.1
  N4: Q2.E, R2.Pin_0, C2.+
  N5: Q2.B, R3.Pin_1, C3.+
  N6: R2.Pin_1, C2.-
  N7: C3.-, R4.Pin_0

notes:
  OUT
