# Fritzing sketch Noise Generator_Dick Cappels (saved by Fritzing 0.9.3b)
breadboards: 1

parts:
  Q1 = NPN-Transistor [package="TO92 [THT]"]
  R1 = Resistor [tolerance=±5% resistance=10k package=THT]
  Q2 = NPN-Transistor [package="TO92 [THT]"]
  C3 = Electrolytic Capacitor [capacitance=1µF package="100 mil [THT, electrolytic]"]
  R4 = Resistor [tolerance=±5% resistance=100k package=THT]
  IC1 = Dual Op-Amp [package=dip08]
  R5 = Resistor [tolerance=±5% resistance=10k package=THT]
  R6 = Resistor [tolerance=±5% resistance=1M package=THT]
  C4 = Ceramic Capacitor [capacitance=100nF package="100 mil [THT, multilayer]"]
  C5 = Ceramic Capacitor [capacitance=100nF package="100 mil [THT, multilayer]"]
  R7 = Resistor [tolerance=±5% resistance=330k package=THT]
  R8 = Resistor [tolerance=±5% resistance=10k package=THT]
  C6 = Electrolytic Capacitor [capacitance=1µF package="100 mil [THT, electrolytic]"]
  R9 = Resistor [tolerance=±5% resistance=10k package=THT]

nets:
  N1: Q1.E, R1.Pin_1, Q2.B, C3.+
  N2: Q1.C, Q2.C
  N3: R1.Pin_0, IC1.A_V+, C5.0
  N4: Q2.E, R4.Pin_1, R5.Pin_1, C4.1, C5.1, R8.Pin_0, R9.Pin_0
  N5: C3.-, R4.Pin_0, IC1.A_+IN
  N6: IC1.A_OUT, R6.Pin_0, C6.+
  N7: IC1.A_-IN, R5.Pin_0, R6.Pin_1
  N8: IC1.A_V-, C4.0
  N9: IC1.B_+IN, C6.-, R9.Pin_1
  N10: IC1.B_-IN, R7.Pin_1, R8.Pin_1
  N11: IC1.B_OUT, R7.Pin_0

notes:
  GND
  V+
  V-
  GND
  OUT2
  OUT1
