# Fritzing sketch W_P_B Noise Generator+AMP (saved by Fritzing 0.9.3b)
breadboards: 2

parts:
  Q1 = NPN-Transistor [package="TO92 [THT]"]
  Q2 = NPN-Transistor [package="TO92 [THT]"]
  R4 = Resistor [tolerance=±5% resistance=100k package=THT]
  IC1 = Dual Op-Amp [package=dip08]
  R5 = Resistor [tolerance=±5% resistance=10k package=THT]
  R6 = Resistor [tolerance=±5% resistance=330k package=THT]
  C4 = Ceramic Capacitor [capacitance=100nF package="100 mil [THT, multilayer]"]
  C5 = Ceramic Capacitor [capacitance=100nF package="100 mil [THT, multilayer]"]
  IC2 = Dual Op-Amp [package=dip08]
  IC3 = Dual Op-Amp [package=dip08]
  R7 = Resistor [tolerance=±5% resistance=10k package=THT]
  C7 = Film/Foil Capacitor [capacitance=100nF voltage=35V package="5mm [THT, pp]"]
  C8 = Film/Foil Capacitor [capacitance=100nF voltage=35V package="5mm [THT, pp]"]
  R8 = Resistor [tolerance=±5% resistance=10k package=THT]
  C9 = Ceramic Capacitor [capacitance=100nF package="100 mil [THT, multilayer]"]
  C10 = Ceramic Capacitor [capacitance=100nF package="100 mil [THT, multilayer]"]
  C11 = Ceramic Capacitor [capacitance=100nF package="100 mil [THT, multilayer]"]
  C12 = Ceramic Capacitor [capacitance=100nF package="100 mil [THT, multilayer]"]
  R9 = Resistor [tolerance=±5% resistance=10k package=THT]
  R10 = Resistor [tolerance=±5% resistance=100k package=THT]
  R11 = Resistor [tolerance=±5% resistance=22k package=THT]
  R12 = Resistor [tolerance=±5% resistance=10k package=THT]
  R13 = Resistor [tolerance=±5% resistance=10k package=THT]
  C13 = Film/Foil Capacitor [capacitance=100nF voltage=35V package="5mm [THT, pp]"]
  C14 = Film/Foil Capacitor [capacitance=100nF voltage=35V package="5mm [THT, pp]"]
  R14 = Resistor [tolerance=±5% resistance=100k package=THT]
  R15 = Resistor [tolerance=±5% resistance=10k package=THT]
  R16 = Resistor [tolerance=±5% resistance=47k package=THT]
  C15 = Electrolytic Capacitor [capacitance=1µF package="100 mil [THT, electrolytic]"]
  C16 = Electrolytic Capacitor [capacitance=1µF package="100 mil [THT, electrolytic]"]
  C17 = Electrolytic Capacitor [capacitance=1µF package="100 mil [THT, electrolytic]"]
  C18 = Electrolytic Capacitor [capacitance=1µF package="100 mil [THT, electrolytic]"]

nets:
  N1: Q1.E, Q2.B, R13.Pin_1, C13.-
  N2: Q1.C, Q2.C
  N3: Q2.E, IC1.A_V-, C4.0, IC2.A_V-, IC3.A_V-, C11.0, C12.0, C16.-, C18.-
  N4: R4.Pin_0, IC1.A_+IN, C13.+
  N5: R4.Pin_1, R5.Pin_1, C4.1, C5.1, IC2.B_+IN, IC3.B_+IN, C7.+, R8.Pin_1, C9.0, C10.0, C11.1, C12.1, R9.Pin_1, R12.Pin_1, R14.Pin_0, R15.Pin_0, C15.-, C16.+, C17.-, C18.+
  N6: IC1.A_OUT, R6.Pin_0, C14.+
  N7: IC1.A_-IN, R5.Pin_0, R6.Pin_1
  N8: IC1.B_+IN, C14.-, R14.Pin_1
  N9: IC1.B_-IN, R15.Pin_1, R16.Pin_1
  N10: IC1.B_OUT, R7.Pin_1, C8.+, R16.Pin_0
  N11: IC1.A_V+, C5.0, IC2.A_V+, IC3.A_V+, C9.1, C10.1, R13.Pin_0, C15.+, C17.+
  N12: IC2.A_OUT, R10.Pin_0
  N13: IC2.A_-IN, R9.Pin_0, R10.Pin_1
  N14: IC2.A_+IN, R7.Pin_0, C7.-
  N15: IC2.B_-IN, IC2.B_OUT
  N16: IC3.A_OUT, R11.Pin_0
  N17: IC3.A_-IN, R11.Pin_1, R12.Pin_0
  N18: IC3.A_+IN, C8.-, R8.Pin_0
  N19: IC3.B_-IN, IC3.B_OUT

notes:
  White
  GND
  V+
  V-
  GND
  Pink
  Blue
